# Fritzing sketch schematics (saved by Fritzing 0.9.6b)
breadboards: 1

parts:
  R1 = Resistor [tolerance=±5% resistance=100k package=THT]
  R2 = Resistor [tolerance=±5% resistance=100k package=THT]
  R3 = Resistor [tolerance=±5% resistance=100k package=THT]
  Q_MAIN = MOSFET-NCHANNEL [package=to220v]
  V1 = DC Power [voltage=5V]
  U1 = NodeMCU V1.0
  R4 = Resistor [tolerance=±5% resistance=100k package=THT]
  R5 = Resistor [tolerance=±5% resistance=100k package=THT]
  U3 = Optocoupler [package=THT]
  R7 = Resistor [tolerance=±5% resistance=10k package=THT]
  Part1 = LCD1602-I2C
  D1 = Rectifier Diode [part_number=1N4001 package="300 mil [THT]"]
  D2 = Rectifier Diode [part_number=1N4001 package="300 mil [THT]"]

nets:
  GND: R1.Pin_0, R2.Pin_0, R3.Pin_0, Q_MAIN.D, U1.GND, R5.Pin_1, Part1.GND
  Row 2: R1.Pin_1, U1.D8
  Row 3: R2.Pin_1, U1.D6
  Row 4: R3.Pin_1, U1.D5
  N1: Q_MAIN.G, R4.Pin_1, U3.Pin_4, D1.cathode
  N2: Q_MAIN.S, V1.V-, R4.Pin_0
  Col 4: V1.V+, U1.Vin, U3.Pin_5, Part1.VCC
  Col 1: U1.D0
  N3: U1.D1, Part1.SCL
  N4: U1.D2, Part1.SDA
  Col 3: U1.D3
  Col 2: U1.D4
  N5: U1.D7, R5.Pin_0, D2.cathode
  N6: U1.RX, U3.Pin_2
  N7: U1.3V3, R7.Pin_1
  N8: U3.Pin_1, R7.Pin_0
  Row 1: D1.anode, D2.anode

custom parts:
  NodeMCU V1.0: ESP8266 based NodeMCU
  LCD1602-I2C: A standard character display, usually with 2x16 characters. Comes in many colors with LCM1602 IIC attached.
